# Fritzing sketch uchino-sensors (saved by Fritzing 0.9.4)
breadboards: 1

parts:
  U1 = ESP-WROOM-02-AE [part_number=ESP-WROOM-02-AE]
  DHT11 = DHT11 basic temperature-humidity sensor [form="♂ (male)" package=THT]
  C2 = Electrolytic Capacitor [capacitance=0.47mF voltage=16V package="200 mil [THT, electrolytic]"]
  C1 = Ceramic Capacitor [capacitance=100nF package="100 mil [THT, multilayer]"]
  U2 = Voltage Regulator - 3.3V [part_number=NJU7223F33]
  4_5V = Battery

nets:
  3.3V: U1.3V3, U1.EN, U1.IO2, U1.IO0, DHT11.VCC, C2.+, U2.OUT
  GND: U1.IO15, U1.GND, DHT11.GND, C2.-, C1.1, U2.GND, 4_5V.-
  N1: U1.IO16, U1.RST
  N2: U1.IO4, DHT11.OUT
  N3: C1.0, U2.IN, 4_5V.+

notes:
  OUT IN GND
  実際は3本

custom parts:
  ESP-WROOM-02-AE: ESP-WROOM-02 with the DIP breakout board by Akizuki-Electronics in Japan. See http://akizukidenshi.com/catalog/g/gK-09758/ for the detauls.
  DHT11 basic temperature-humidity sensor: The DHT11 is a basic, ultra low-cost digital temperature and humidity sensor. It uses a capacitive humidity sensor and a thermistor to measure the surrounding air, and spits out a digital signal on the data pin (no analog input pins needed). Its fairly simple to use, but requires careful timing to grab data. The only real downside of this sensor is you can only get new data from it once every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
  Voltage Regulator - 3.3V: 3.3V DC Voltage Regulator
